// Logisim project LC-2200-16.circ as structural Verilog: 5 circuits, main circuit main
module main (
  input  in_1,
  input  in_2,
  input  in_3,
  input  in_4,
  input  in_5,
  input  in_6,
  input  in_7,
  input  in_8,
  input  in_9,
  input  in_10,
  input  in_11,
  input  in_12,
  input  in_13,
  input  in_14,
  input  in_15,
  input  in_16,
  input  in_17,
  input  in_18,
  output [15:0] BUS,
  output [15:0] RegVal,
  output Z,
  output [2:0] OpCode,
  output [3:0] RegNum
);

  wire Clk, nor_1_out;
  wire [12:0] IRVal;
  wire [15:0] A_q, B_q, bit_extender_1_out, MAR_q, n16_bit_alu_1_out_4, PC_q, ram_2_data;

  Register #(.width(16)) PC (.D(BUS), .en(in_2), .Q(PC_q), .clk(Clk), .clr(in_18));
  Clock clock_1 (.out(Clk));
  assign BUS = in_1 ? PC_q : 16'bz;  // Controlled_Buffer controlled_buffer_1
  Register #(.width(16)) A (.D(BUS), .en(in_5), .Q(A_q), .clk(Clk), .clr(in_18));
  _16_bit_ALU u_16_bit_alu_1 (.in_1(B_q), .in_2(A_q), .in_3({in_6, in_3}), .out_4(n16_bit_alu_1_out_4));
  assign BUS = in_4 ? n16_bit_alu_1_out_4 : 16'bz;  // Controlled_Buffer controlled_buffer_2
  Register #(.width(16)) B (.D(BUS), .en(in_8), .Q(B_q), .clk(Clk), .clr(in_18));
  RAM #(.addrWidth(4), .dataWidth(16), .bus("separate")) ram_1 (
    .addr(RegNum), .din(BUS), .data(RegVal), .str(in_17), .clk(Clk), .ld(1'b1), .clr(in_18));  // open: sel
  assign BUS = in_7 ? RegVal : 16'bz;  // Controlled_Buffer controlled_buffer_3
  Register #(.width(16)) MAR (.D(BUS), .en(in_11), .Q(MAR_q), .clk(Clk), .clr(in_18));
  RAM #(.addrWidth(16), .dataWidth(16), .bus("separate")) ram_2 (
    .addr(MAR_q), .din(BUS), .data(ram_2_data), .str(in_15), .clk(Clk), .ld(1'b1), .clr(in_18));  // open: sel
  assign BUS = in_10 ? ram_2_data : 16'bz;  // Controlled_Buffer controlled_buffer_4
  Multiplexer #(.select(2), .width(4), .disabled(0), .enable("false")) multiplexer_1 (
    .in0(IRVal[12:9]), .in1(IRVal[8:5]), .in2(IRVal[3:0]), .out(RegNum), .sel({in_12, in_9}));  // open: in3
  Register #(.width(16)) IR (.D(BUS), .en(in_14), .Q({OpCode, IRVal}), .clk(Clk), .clr(in_18));
  assign bit_extender_1_out = {{11{IRVal[4]}}, IRVal[4:0]};  // Bit_Extender bit_extender_1
  Register #(.width(1)) u_Z (.D(nor_1_out), .en(in_16), .Q(Z), .clk(Clk), .clr(in_18));
  nor nor_1 (nor_1_out, BUS[15], BUS[14], BUS[13], BUS[12], BUS[11], BUS[10], BUS[9], BUS[8], BUS[6], BUS[5], BUS[4], BUS[3], BUS[2], BUS[1], BUS[0], BUS[7]);
  assign BUS = in_13 ? bit_extender_1_out : 16'bz;  // Controlled_Buffer controlled_buffer_5

  // Other names for the same wires on the sheet: ALULo = in_3; ALUSel[1:0] = {in_6, in_3}; ALUHi = in_6; Clr = in_18;
  //   DrALU = in_4; DrMEM = in_10; DrOFF = in_13; DrPC = in_1; DrREG = in_7; LdA = in_5; LdB = in_8; LdIR = in_14;
  //   LdMAR = in_11; LdPC = in_2; LdZ = in_16; Offset[4:0] = IRVal[4:0]; RZ[3:0] = IRVal[3:0]; IRVal[15:13] = OpCode;
  //   RegSel[1:0] = {in_12, in_9}; RegSelLo = in_9; RegSelHi = in_12; RX[3:0] = IRVal[12:9]; RY[3:0] = IRVal[8:5];
  //   WrMEM = in_15; WrREG = in_17
endmodule

module _1_bit_adder (
  input  in_1,
  input  in_2,
  input  in_3,
  output out_4,
  output out_5
);

  wire and_1_out, and_2_out, xor_1_out;

  and and_1 (and_1_out, in_1, in_2);
  xor xor_1 (xor_1_out, in_1, in_2);
  and and_2 (and_2_out, xor_1_out, in_3);
  xor xor_2 (out_4, xor_1_out, in_3);
  or or_1 (out_5, and_2_out, and_1_out);

  // Other names for the same wires on the sheet: A = in_1; B = in_2; C_IN = in_3; C_OUT = out_5; S = out_4
endmodule

module _16_bit_adder (
  input  [15:0] in_1,
  input  [15:0] in_2,
  input  in_3,
  output [15:0] out_4,
  output out_5
);

  wire n1_bit_adder_1_out_5, n1_bit_adder_3_out_5, n1_bit_adder_4_out_5, n1_bit_adder_5_out_5,
       n1_bit_adder_6_out_5, n1_bit_adder_7_out_5, n1_bit_adder_8_out_5, n1_bit_adder_9_out_5,
       n1_bit_adder_10_out_5, n1_bit_adder_11_out_5, n1_bit_adder_12_out_5, n1_bit_adder_13_out_5,
       n1_bit_adder_14_out_5, n1_bit_adder_15_out_5, n1_bit_adder_16_out_5;

  _1_bit_adder u_1_bit_adder_1 (
    .in_1(n1_bit_adder_4_out_5), .in_2(in_2[14]), .in_3(in_1[14]), .out_4(out_4[14]),
    .out_5(n1_bit_adder_1_out_5));
  _1_bit_adder u_1_bit_adder_2 (
    .in_1(n1_bit_adder_1_out_5), .in_2(in_2[15]), .in_3(in_1[15]), .out_4(out_4[15]), .out_5(out_5));
  _1_bit_adder u_1_bit_adder_3 (
    .in_1(n1_bit_adder_6_out_5), .in_2(in_2[12]), .in_3(in_1[12]), .out_4(out_4[12]),
    .out_5(n1_bit_adder_3_out_5));
  _1_bit_adder u_1_bit_adder_4 (
    .in_1(n1_bit_adder_3_out_5), .in_2(in_2[13]), .in_3(in_1[13]), .out_4(out_4[13]),
    .out_5(n1_bit_adder_4_out_5));
  _1_bit_adder u_1_bit_adder_5 (
    .in_1(n1_bit_adder_7_out_5), .in_2(in_2[10]), .in_3(in_1[10]), .out_4(out_4[10]),
    .out_5(n1_bit_adder_5_out_5));
  _1_bit_adder u_1_bit_adder_6 (
    .in_1(n1_bit_adder_5_out_5), .in_2(in_2[11]), .in_3(in_1[11]), .out_4(out_4[11]),
    .out_5(n1_bit_adder_6_out_5));
  _1_bit_adder u_1_bit_adder_7 (
    .in_1(n1_bit_adder_8_out_5), .in_2(in_2[9]), .in_3(in_1[9]), .out_4(out_4[9]),
    .out_5(n1_bit_adder_7_out_5));
  _1_bit_adder u_1_bit_adder_8 (
    .in_1(n1_bit_adder_10_out_5), .in_2(in_2[8]), .in_3(in_1[8]), .out_4(out_4[8]),
    .out_5(n1_bit_adder_8_out_5));
  _1_bit_adder u_1_bit_adder_9 (
    .in_1(n1_bit_adder_12_out_5), .in_2(in_2[6]), .in_3(in_1[6]), .out_4(out_4[6]),
    .out_5(n1_bit_adder_9_out_5));
  _1_bit_adder u_1_bit_adder_10 (
    .in_1(n1_bit_adder_9_out_5), .in_2(in_2[7]), .in_3(in_1[7]), .out_4(out_4[7]),
    .out_5(n1_bit_adder_10_out_5));
  _1_bit_adder u_1_bit_adder_11 (
    .in_1(n1_bit_adder_13_out_5), .in_2(in_2[4]), .in_3(in_1[4]), .out_4(out_4[4]),
    .out_5(n1_bit_adder_11_out_5));
  _1_bit_adder u_1_bit_adder_12 (
    .in_1(n1_bit_adder_11_out_5), .in_2(in_2[5]), .in_3(in_1[5]), .out_4(out_4[5]),
    .out_5(n1_bit_adder_12_out_5));
  _1_bit_adder u_1_bit_adder_13 (
    .in_1(n1_bit_adder_14_out_5), .in_2(in_2[3]), .in_3(in_1[3]), .out_4(out_4[3]),
    .out_5(n1_bit_adder_13_out_5));
  _1_bit_adder u_1_bit_adder_14 (
    .in_1(n1_bit_adder_15_out_5), .in_2(in_2[2]), .in_3(in_1[2]), .out_4(out_4[2]),
    .out_5(n1_bit_adder_14_out_5));
  _1_bit_adder u_1_bit_adder_15 (
    .in_1(n1_bit_adder_16_out_5), .in_2(in_2[1]), .in_3(in_1[1]), .out_4(out_4[1]),
    .out_5(n1_bit_adder_15_out_5));
  _1_bit_adder u_1_bit_adder_16 (
    .in_1(in_3), .in_2(in_2[0]), .in_3(in_1[0]), .out_4(out_4[0]), .out_5(n1_bit_adder_16_out_5));

  // Other names for the same wires on the sheet: A[15:0] = in_1; B[15:0] = in_2; C_IN = in_3; C_OUT = out_5;
  //   S[15:0] = out_4
endmodule

module _16_bit_ALU (
  input  [15:0] in_1,
  input  [15:0] in_2,
  input  [1:0] in_3,
  output [15:0] out_4
);

  wire [15:0] and_1_out, n16_bit_adder_1_out_4, n16_bit_adder_2_out_4, nand_1_out, not_1_out;

  _16_bit_adder u_16_bit_adder_1 (.in_1(in_1), .in_2(in_2), .in_3(1'b0), .out_4(n16_bit_adder_1_out_4));  // open: out_5
  assign and_1_out = in_1 & not_1_out;  // AND_Gate and_1, 16 bits wide
  assign not_1_out = ~in_2;  // NOT_Gate not_1, 16 bits wide
  _16_bit_adder u_16_bit_adder_2 (
    .in_1(in_1), .in_2(16'h1), .in_3(1'b0), .out_4(n16_bit_adder_2_out_4));  // open: out_5
  assign nand_1_out = ~(in_1 & in_2);  // NAND_Gate nand_1, 16 bits wide
  Multiplexer #(.select(2), .width(16), .disabled(0), .enable("false")) multiplexer_1 (
    .in0(n16_bit_adder_1_out_4), .in1(nand_1_out), .in2(and_1_out), .in3(n16_bit_adder_2_out_4), .out(out_4),
    .sel(in_3));

  // Other names for the same wires on the sheet: A[15:0] = in_1; B[15:0] = in_2; Out[15:0] = out_4; Sel[1:0] = in_3

  // Notes on the sheet:
  //   Add
  //   Sub
  //   Incr
  //   Nand
endmodule

module microcontroller (
);

  wire [5:0] multiplexer_1_out, register_1_q;

  Multiplexer #(.select(2), .width(6), .disabled(0), .enable("false")) multiplexer_1 (.out(multiplexer_1_out));  // open: in0, in1, in2, in3, sel
  Register #(.width(6)) register_1 (.D(multiplexer_1_out), .Q(register_1_q));  // open: en, clk, clr
  ROM #(.addrWidth(6), .dataWidth(25)) rom_1 (.addr(register_1_q));  // open: data, sel
  main datapath ();  // open: in_1, in_2, in_3, BUS, in_4, in_5, in_6, in_7, in_8, in_9, RegVal, in_10, in_11, in_12, in_13, in_14, in_15, Z, in_16, in_17, OpCode, RegNum, in_18
endmodule
